# Fritzing sketch Schematic (saved by Fritzing 0.7.12b)
breadboards: 1

parts:
  Arduino1 = Arduino
  Part2 = Bluetooth Mate Silver
  LED1 = white smd LED [package="0603 [SMD]"]
  R1 = 470 Ω Resistor [package=THT]

nets:
  GND: Arduino1.GND, Part2.GND
  N1: Arduino1.D3, R1.Pin_0
  N2: Arduino1.D1TX, Part2.RX_5V
  N3: Arduino1.D0RX, Part2.TX_5V
  +5V: Arduino1.+5V, Part2.VCC
  N4: LED1.anode, R1.Pin_1
